# Fritzing sketch Motion Detection Alarm (saved by Fritzing 0.9.3b)
breadboards: 1

parts:
  Part1 = Arduino Uno (Rev3)
  SP1 = SPEAKER [package=pcb_mount_speaker]
  R1 = Resistor [tolerance=±5% resistance=30 package=THT]
  J1 = Infrared Proximity Sensor
  LED1 = LED - 5mm [color="Red (633nm)" package="5 mm [THT]"]
  R2 = Resistor [tolerance=±5% resistance=220 package=THT]
  Q1 = NPN-Transistor [package="TO92 [THT]"]
  R3 = Resistor [tolerance=±5% resistance=10k package=THT]

nets:
  N1: Part1.D9_PWM, R3.Pin_0
  N2: Part1.D13/SCK, R2.Pin_0
  GND: Part1.GND, J1.GND, LED1.cathode
  N3: Part1.D7, J1.Vout, Q1.E
  5V: Part1.5V, R1.Pin_0, J1.Vcc
  N4: SP1.+, R1.Pin_1
  N5: SP1.-, Q1.C
  N6: LED1.anode, R2.Pin_1
  N7: Q1.B, R3.Pin_1

// code stored in the sketch: Motion Detector Alarm.ino
int ledPin = 13;
int pirPin = 7;
int speakerPin = 9;

void setup() {
  Serial.begin(9600);
  pinMode(ledPin, OUTPUT);
  pinMode(pirPin, INPUT);
  digitalWrite(ledPin, LOW);
  pinMode(speakerPin,OUTPUT);
}

void loop() {
  int pirVal = digitalRead(pirPin);
  if(pirVal == 1)
  {
    //Plays brief audible sound
    tone(speakerPin,262,2);
    //Strobes the LED
    for (int i=0; i<10; i++)
    {
      digitalWrite(ledPin,HIGH);
      digitalWrite(ledPin,LOW);
    } 
  }
}
